# Fritzing sketch domo_poules (saved by Fritzing 0.9.3b)
breadboards: 1

parts:
  Composant1 = Arduino Micro (Rev3)
  S1 = Pushbutton [package="[THT]"]
  S2 = Pushbutton [package="[THT]"]
  R2 = Resistor [tolerance=±5% resistance=10k package=THT]
  R1 = Resistor [tolerance=±5% resistance=10k package=THT]
  M1 = DC Motor  # not connected
  RHT1 = Humidity and Temperature Sensor RHT03
  T1 = LM35 Temperature Sensor [package="TO92 [THT]"]  # not connected
  R3 = Photocell (LDR) [package=THT]  # not connected
  R4 = Resistor [tolerance=±5% resistance=220 package=THT]

nets:
  N1: Composant1.GND, R2.Pin_1, R1.Pin_1, RHT1.GND_2
  5V: Composant1.5V, S1.Pin_3, S1.Pin_4, S2.Pin_3, S2.Pin_4, RHT1.Vcc, R4.Pin_0
  N2: S1.Pin_1, S1.Pin_2, R1.Pin_0
  N3: S2.Pin_1, S2.Pin_2, R2.Pin_0
  N4: RHT1.Data-signal, R4.Pin_1

notes:
  moteur à brancher via un module L293D
